# Fritzing sketch RCV1 (saved by Fritzing 0.9.4)
breadboards: 1

parts:
  U1 = ESP32-38PinWide [part_number=ESP32-38PinWide]
  IC2 = AE-DRV8835-S [package="DIP (Dual Inline) [THT]"]
  M1 = DC Motor
  M3 = DC Motor
  J1 = Piezo Speaker
  BAT1 = BC9VPC [package=bc9vpc]
  Stepdown_Voltage1 = Polulu Stepdown Voltage [part_number=D24V25F3,D24V25F5]
  S1 = SPST Switch [package=switch-spdt]
  J2 = Basic Servo

nets:
  N1: U1.3.3, IC2.VCC
  N2: U1.GPIO36, IC2.MODE
  N3: U1.GPIO39, J2.pulse
  N4: U1.GPIO25, J1.pin2
  N5: U1.GPIO27, IC2.AIN1
  N6: U1.GPIO14, IC2.AIN2
  N7: U1.GPIO12, IC2.BIN1
  GND: U1.GND, IC2.GND, J1.pin1, Stepdown_Voltage1.GND#3, J2.gnd
  N8: U1.GPIO13, IC2.BIN2
  VIN: U1.VIN, Stepdown_Voltage1.VOut, J2.vcc
  N9: IC2.AOUT1, M3.pin_2
  N10: IC2.AOUT2, M3.pin_1
  N11: IC2.BOUT1, M1.pin_2
  N12: IC2.BOUT2, M1.pin_1
  N13: BAT1.V+, Stepdown_Voltage1.VIn, S1.O
  GND_2: BAT1.V-, Stepdown_Voltage1.GND#2, S1.S
  N14: Stepdown_Voltage1.EN, S1.P

custom parts:
  ESP32-38PinWide: Generic 38-Pin ESP32 with wide format (only access to one side of pins on a breadboard) based on Stephen Lilley's HiLetgo ESP-WROOM-32 ESP32 ESP-32S Development Board.
  AE-DRV8835-S: A DRV8835 breakout board by Akizuki Denshi Tsusho Co.,Ltd.
  Polulu Stepdown Voltage: Polulu Stepdown Voltage 3V3 or 5V, 2.5A
